// Logisim project ALU.circ as structural Verilog: 3 circuits, main circuit alu
module alu (
  input  [31:0] X,
  input  [31:0] Y,
  input  [3:0] AluOP,
  output Signed_Overflow,
  output [31:0] Result,
  output [31:0] Result2,
  output Unsigned_Overflow,
  output Equal
);

  wire comparator_1_lt, comparator_2_gt;
  wire [1:0] adder_with_overflow_detection_1_cf, subtractor_with_overflow_detection_1_cf;
  wire [31:0] adder_with_overflow_detection_1_result, and_1_out, bit_extender_1_out, bit_extender_2_out,
       divider_1_out, divider_1_rem, multiplier_1_cout, multiplier_1_out, not_1_out, or_1_out, or_2_out,
       shifter_1_out, shifter_2_out, shifter_3_out, subtractor_with_overflow_detection_1_result, xor_1_out;

  // Probe on X
  // Probe on X
  // Probe on X
  // Probe on Y
  // Probe on Y
  // Probe on Y
  Shifter #(.width(32)) shifter_1 (.in(X), .\dist (Y[4:0]), .out(shifter_1_out));
  Shifter #(.shift("ar"), .width(32)) shifter_2 (.in(X), .\dist (Y[4:0]), .out(shifter_2_out));
  Multiplexer #(.select(4), .width(2)) multiplexer_1 (
    .in0(2'b00), .in1(2'b00), .in2(2'b00), .in3(2'b00), .in4(2'b00),
    .in5(adder_with_overflow_detection_1_cf), .in6(subtractor_with_overflow_detection_1_cf), .in7(2'b00),
    .in8(2'b00), .in9(2'b00), .in10(2'b00), .in11(2'b00), .in12(2'b00), .in13(2'b00), .in14(2'b00),
    .in15(2'b00), .out({Signed_Overflow, Unsigned_Overflow}), .sel(AluOP));
  Shifter #(.shift("lr"), .width(32)) shifter_3 (.in(X), .\dist (Y[4:0]), .out(shifter_3_out));
  Multiplier #(.width(32)) multiplier_1 (.a(X), .b(Y), .out(multiplier_1_out), .cout(multiplier_1_cout));  // open: cin
  Divider #(.width(32)) divider_1 (.a(X), .b(Y), .out(divider_1_out), .rem(divider_1_rem));  // open: upper
  Adder_with_Overflow_Detection adder_with_overflow_detection_1 (
    .X(X), .Y(Y), .Result(adder_with_overflow_detection_1_result),
    .OVF(adder_with_overflow_detection_1_cf[1]), .CF(adder_with_overflow_detection_1_cf[0]));  // open: Cin
  Subtractor_with_Overflow_Detection subtractor_with_overflow_detection_1 (
    .X(X), .Y(Y), .Result(subtractor_with_overflow_detection_1_result),
    .OVF(subtractor_with_overflow_detection_1_cf[1]), .CF(subtractor_with_overflow_detection_1_cf[0]));  // open: Bin
  assign and_1_out = X & Y;  // AND_Gate and_1, 32 bits wide
  assign or_1_out = X | Y;  // OR_Gate or_1, 32 bits wide
  assign xor_1_out = X ^ Y;  // XOR_Gate xor_1, 32 bits wide
  assign or_2_out = X | Y;  // OR_Gate or_2, 32 bits wide
  Comparator #(.width(32)) comparator_1 (.a(X), .b(Y), .lt(comparator_1_lt));  // open: gt, eq
  Comparator #(.width(32)) comparator_2 (.a(X), .b(Y), .gt(comparator_2_gt), .eq(Equal));  // open: lt
  assign not_1_out = ~or_2_out;  // NOT_Gate not_1, 32 bits wide
  assign bit_extender_1_out = {{31{1'b0}}, comparator_2_gt};  // Bit_Extender bit_extender_1
  // Probe on AluOP
  assign bit_extender_2_out = {{31{1'b0}}, comparator_1_lt};  // Bit_Extender bit_extender_2
  Multiplexer #(.select(4), .width(32)) multiplexer_2 (
    .in0({32{1'b0}}), .in1({32{1'b0}}), .in2({32{1'b0}}), .in3(multiplier_1_cout), .in4(divider_1_rem),
    .in5({32{1'b0}}), .in6({32{1'b0}}), .in7({32{1'b0}}), .in8({32{1'b0}}), .in9({32{1'b0}}),
    .in10({32{1'b0}}), .in11({32{1'b0}}), .in12({32{1'b0}}), .in13({32{1'b0}}), .in14({32{1'b0}}),
    .in15({32{1'b0}}), .out(Result2), .sel(AluOP));
  Multiplexer #(.select(4), .width(32)) multiplexer_3 (
    .in0(shifter_1_out), .in1(shifter_2_out), .in2(shifter_3_out), .in3(multiplier_1_out),
    .in4(divider_1_out), .in5(adder_with_overflow_detection_1_result),
    .in6(subtractor_with_overflow_detection_1_result), .in7(and_1_out), .in8(or_1_out), .in9(xor_1_out),
    .in10(not_1_out), .in11(bit_extender_2_out), .in12(bit_extender_1_out), .in13({32{1'b0}}),
    .in14({32{1'b0}}), .in15({32{1'b0}}), .out(Result), .sel(AluOP));
  // Probe on Result
  // Probe on Result
  // Probe on Result2

  // Other names for the same wires on the sheet: CF = Unsigned_Overflow; OVF = Signed_Overflow; S[3:0] = AluOP

  // Notes on the sheet:
  //   32-BIT ALU
  //   INPUT
  //   DEBUG
  //   OUTPUT
endmodule

module Adder_with_Overflow_Detection (
  input  [31:0] X,
  input  [31:0] Y,
  input  Cin,
  output OVF,
  output [31:0] Result,
  output CF
);

  wire adder_1_cout;

  // Probe on X
  // Probe on Y
  Adder #(.width(31)) adder_1 (.a(X[30:0]), .b(Y[30:0]), .out(Result[30:0]), .cin(Cin), .cout(adder_1_cout));
  Adder #(.width(1)) adder_2 (.a(X[31]), .b(Y[31]), .out(Result[31]), .cin(adder_1_cout), .cout(CF));
  xor xor_1 (OVF, adder_1_cout, CF);
  // Probe on Result

  // Notes on the sheet:
  //   32-BIT ADDER WITH OVERLOW DETECTION
  //   Carry In
  //   INPUT
  //   OUTPUT
  //   Overflow Flag
  //   Carry Flag
endmodule

module Subtractor_with_Overflow_Detection (
  input  [31:0] X,
  input  [31:0] Y,
  input  Bin,
  output OVF,
  output [31:0] Result,
  output CF
);

  wire subtractor_1_bout;

  // Probe on X
  // Probe on Y
  Subtractor #(.width(31)) subtractor_1 (
    .a(X[30:0]), .b(Y[30:0]), .out(Result[30:0]), .bin(Bin), .bout(subtractor_1_bout));
  Subtractor #(.width(1)) subtractor_2 (.a(X[31]), .b(Y[31]), .out(Result[31]), .bin(subtractor_1_bout), .bout(CF));
  xor xor_1 (OVF, subtractor_1_bout, CF);
  // Probe on Result

  // Notes on the sheet:
  //   BorrowIn
  //   32-BIT SUBTRACTOR WITH OVERLOW DETECTION
  //   INPUT
  //   OUTPUT
  //   Overflow Flag
  //   Carry Flag
endmodule
