// Logisim project CPU.circ as structural Verilog: 1 circuit, main circuit CPU
module CPU (
);

  wire ALUSrc, and_1_out, and_2_out, BneOrBeq, Branch, clk, clock_1_out, Equal, ExpBlock, ExpSrc0, ExpSrc1,
       ExpSrc2, ExRegWrite, Halt, HasExp, instruction_statistics_1_i, instruction_statistics_1_j,
       instruction_statistics_1_r, IsCOP0, IsEret, IsJAL, IsJR, IsShamt, IsSyscall, Jump, MemRead, MemtoReg,
       MemWrite, multiplexer_4_out, multiplexer_10_out, not_1_out, not_2_out, not_3_out, not_4_out,
       not_5_out, or_1_out, RegDst, RegWrite, xor_1_out, ZeroExtend;
  wire [3:0] adder_1_out_2, ALUop, syscall_decoder_1_hex_2, syscall_decoder_1_hex_3, syscall_decoder_1_hex_4,
       syscall_decoder_1_hex_5, syscall_decoder_1_hex_6, syscall_decoder_1_hex_7;
  wire [4:0] multiplexer_6_out, multiplexer_7_out, multiplexer_8_out, multiplexer_9_out;
  wire [5:0] multiplexer_5_out;
  wire [7:0] syscall_decoder_1_hex;
  wire [8:0] demultiplexer_1_out0, demultiplexer_1_out1;
  wire [25:0] multiplexer_5_out_2;
  wire [27:0] adder_1_out;
  wire [31:0] adder_2_out, adder_3_out, alu_1_result, bit_extender_1_out, counter_1_q, counter_2_q,
       counter_3_q, cp0_1_dout, cp0_1_pcout, Cycle_q, immediate_extender_1_result, multiplexer_1_out,
       multiplexer_2_out, multiplexer_11_out, multiplexer_12_out, multiplexer_13_out, multiplexer_14_out,
       multiplexer_15_out, multiplexer_16_out, multiplexer_17_out, multiplexer_18_out, multiplexer_19_out,
       PC_q, PCBuffer_q, ram_1_dout, regfile_1_r1, regfile_1_r2, rom_1_data, ROMA_data, shifter_1_out;

  Multiplexer #(.width(32)) multiplexer_1 (
    .in0(multiplexer_18_out), .in1(cp0_1_pcout), .out(multiplexer_1_out), .sel(and_1_out));
  and and_1 (and_1_out, IsEret, IsCOP0);
  Multiplexer #(.width(32)) multiplexer_2 (
    .in0(32'h800), .in1(multiplexer_1_out), .out(multiplexer_2_out), .sel(not_1_out));
  not not_1 (not_1_out, HasExp);
  or or_1 (or_1_out, HasExp, and_1_out);
  Multiplexer multiplexer_3 (.in0(clock_1_out), .in1(1'b1), .out(clk), .sel(Halt));
  Clock clock_1 (.out(clock_1_out));
  Counter #(.max('hffffffff), .width(32)) Cycle (.Q(Cycle_q), .clk(clk));  // open: load, D, count, carry, up, clr
  // Probe on Cycle_q
  Register #(.width(32)) PC (.D(multiplexer_2_out), .Q(PC_q), .clk(multiplexer_4_out));  // open: en, clr
  Multiplexer multiplexer_4 (.in0(clk), .in1(not_2_out), .out(multiplexer_4_out), .sel(or_1_out));
  not not_2 (not_2_out, clk);
  Demultiplexer #(.width(9)) demultiplexer_1 (
    .out0(demultiplexer_1_out0), .out1(demultiplexer_1_out1), .in(PC_q[10:2]), .sel(PC_q[11]));
  Counter #(.max('hffffffff), .width(32)) counter_1 (
    .count(instruction_statistics_1_j), .Q(counter_1_q), .clk(clk));  // open: load, D, carry, up, clr
  // Probe on counter_1_q
  ROM #(.addrWidth(9), .dataWidth(32)) ROMA (.addr(demultiplexer_1_out0), .data(ROMA_data));
  ROM #(.addrWidth(9), .dataWidth(32)) rom_1 (.addr(demultiplexer_1_out1), .data(rom_1_data));
  Adder #(.width(32)) adder_1 (.a(32'h4), .b(PC_q), .out({adder_1_out_2, adder_1_out}));  // open: cin, cout
  Counter #(.max('hffffffff), .width(32)) counter_2 (
    .count(instruction_statistics_1_r), .Q(counter_2_q), .clk(clk));  // open: load, D, carry, up, clr
  // Probe on counter_2_q
  Counter #(.max('hffffffff), .width(32)) counter_3 (
    .count(instruction_statistics_1_i), .Q(counter_3_q), .clk(clk));  // open: load, D, carry, up, clr
  Instruction_Statistics instruction_statistics_1 (
    .op2(multiplexer_5_out[3]), .op3(multiplexer_5_out[2]), .op4(multiplexer_5_out[1]),
    .op0(multiplexer_5_out[5]), .op5(multiplexer_5_out[0]), .op1(multiplexer_5_out[4]),
    .r(instruction_statistics_1_r), .j(instruction_statistics_1_j), .i(instruction_statistics_1_i));
  // Probe on counter_3_q
  Adder #(.width(32)) adder_2 (.a(PC_q), .b(32'h4), .out(adder_2_out));  // open: cin, cout
  Register #(.width(32)) PCBuffer (.D(PC_q), .Q(PCBuffer_q), .clk(HasExp));  // open: en, clr
  Multiplexer #(.width(32)) multiplexer_5 (
    .in0(ROMA_data), .in1(rom_1_data), .out({multiplexer_5_out, multiplexer_5_out_2}), .sel(PC_q[11]));
  Control_Unit control_unit_1 (
    .op(multiplexer_5_out), .Funct(multiplexer_5_out_2[5:0]), .ALUop(ALUop), .IsJAL(IsJAL),
    .IsShamt(IsShamt), .MemtoReg(MemtoReg), .RegWrite(RegWrite), .BneOrBeq(BneOrBeq), .ALUSrc(ALUSrc),
    .IsSyscall(IsSyscall), .ZeroExtend(ZeroExtend), .MemRead(MemRead), .MemWrite(MemWrite), .Jump(Jump),
    .Branch(Branch), .RegDst(RegDst), .IsJR(IsJR), .IsCOP0(IsCOP0));  // open: ReadRs, ReadRt
  Multiplexer #(.width(5)) multiplexer_6 (
    .in0(multiplexer_5_out_2[20:16]), .in1(multiplexer_5_out_2[15:11]), .out(multiplexer_6_out), .sel(RegDst));
  immediate_extender immediate_extender_1 (
    .in_2(multiplexer_5_out_2[15:0]), .ZeroExtend(ZeroExtend), .result(immediate_extender_1_result));
  Multiplexer #(.width(5)) multiplexer_7 (
    .in0(multiplexer_6_out), .in1({5{1'b1}}), .out(multiplexer_7_out), .sel(IsJAL));
  Multiplexer #(.width(5)) multiplexer_8 (
    .in0(multiplexer_5_out_2[25:21]), .in1(5'b00010), .out(multiplexer_8_out), .sel(IsSyscall));
  Multiplexer #(.width(5)) multiplexer_9 (
    .in0(multiplexer_5_out_2[20:16]), .in1(5'b00100), .out(multiplexer_9_out), .sel(IsSyscall));
  CP0 cp0_1 (
    .in_6({multiplexer_5_out, multiplexer_5_out_2}), .ExpSrc1(ExpSrc1), .ExpSrc2(ExpSrc2), .ExpSrc0(ExpSrc0),
    .in_2(clk), .Enable(IsCOP0), .PCin(PCBuffer_q), .Din(regfile_1_r2), .PCout(cp0_1_pcout),
    .Dout(cp0_1_dout), .ExRegWrite(ExRegWrite), .ExpBlock(ExpBlock), .HasExp(HasExp), .IsRet(IsEret));
  RegFile regfile_1 (
    .WE(multiplexer_10_out), .clk(clk), .R1i(multiplexer_8_out), .R2i(multiplexer_9_out),
    .RW(multiplexer_7_out), .Din(multiplexer_11_out), .R1(regfile_1_r1), .R2(regfile_1_r2));  // open: a0, v0
  Multiplexer multiplexer_10 (.in0(RegWrite), .in1(ExRegWrite), .out(multiplexer_10_out), .sel(IsCOP0));
  Multiplexer #(.width(32)) multiplexer_11 (
    .in0(cp0_1_dout), .in1(multiplexer_12_out), .out(multiplexer_11_out), .sel(not_3_out));
  not not_3 (not_3_out, IsCOP0);
  Multiplexer #(.width(32)) multiplexer_12 (
    .in0(adder_2_out), .in1(multiplexer_19_out), .out(multiplexer_12_out), .sel(not_4_out));
  not not_4 (not_4_out, IsJAL);
  alu alu_1 (
    .X(multiplexer_14_out), .Y(multiplexer_15_out), .AluOP(ALUop), .Result(alu_1_result), .Equal(Equal));  // open: Result2, Unsigned_Overflow, Signed_Overflow
  syscall_decoder syscall_decoder_1 (
    .clk(clk), .Enable(IsSyscall), .v0(regfile_1_r1), .a0(regfile_1_r2), .Halt(Halt),
    .Hex({syscall_decoder_1_hex_7, syscall_decoder_1_hex_6, syscall_decoder_1_hex_5, syscall_decoder_1_hex_4, syscall_decoder_1_hex_3, syscall_decoder_1_hex_2, syscall_decoder_1_hex}));
  Shifter #(.width(32)) shifter_1 (.in(immediate_extender_1_result), .\dist (5'b00010), .out(shifter_1_out));
  Multiplexer #(.width(32)) multiplexer_13 (
    .in0(regfile_1_r2), .in1(immediate_extender_1_result), .out(multiplexer_13_out), .sel(ALUSrc));
  assign bit_extender_1_out = {{27{1'b0}}, multiplexer_5_out_2[10:6]};  // Bit_Extender bit_extender_1
  xor xor_1 (xor_1_out, Equal, BneOrBeq);
  Multiplexer #(.width(32)) multiplexer_14 (
    .in0(regfile_1_r1), .in1(regfile_1_r2), .out(multiplexer_14_out), .sel(IsShamt));
  Multiplexer #(.width(32)) multiplexer_15 (
    .in0(multiplexer_13_out), .in1(bit_extender_1_out), .out(multiplexer_15_out), .sel(IsShamt));
  Adder #(.width(32)) adder_3 (
    .a({adder_1_out_2, adder_1_out}), .b(shifter_1_out), .out(adder_3_out));  // open: cin, cout
  and and_2 (and_2_out, Branch, xor_1_out);
  Hex_Digit_Display hex_digit_display_1 (.value(syscall_decoder_1_hex_7));  // open: dp
  Multiplexer #(.width(32)) multiplexer_16 (
    .in0({adder_1_out_2, adder_1_out}), .in1(adder_3_out), .out(multiplexer_16_out), .sel(and_2_out));
  not not_5 (not_5_out, Jump);
  Hex_Digit_Display hex_digit_display_2 (.value(syscall_decoder_1_hex_6));  // open: dp
  Hex_Digit_Display hex_digit_display_3 (.value(syscall_decoder_1_hex_5));  // open: dp
  RAM #(.addrWidth(10), .dataWidth(32)) ram_1 (
    .addr(alu_1_result[11:2]), .we(MemWrite), .oe(MemRead), .clk(clk), .din(regfile_1_r2), .dout(ram_1_dout));
  Button button_1 (.out(ExpSrc0));
  Multiplexer #(.width(32)) multiplexer_17 (
    .in0({adder_1_out_2, multiplexer_5_out_2, 2'b00}), .in1(multiplexer_16_out), .out(multiplexer_17_out),
    .sel(not_5_out));
  Hex_Digit_Display hex_digit_display_4 (.value(syscall_decoder_1_hex_4));  // open: dp
  Hex_Digit_Display hex_digit_display_5 (.value(syscall_decoder_1_hex_3));  // open: dp
  Button button_2 (.out(ExpSrc1));
  Multiplexer #(.width(32)) multiplexer_18 (
    .in0(multiplexer_17_out), .in1(regfile_1_r1), .out(multiplexer_18_out), .sel(IsJR));
  Hex_Digit_Display hex_digit_display_6 (.value(syscall_decoder_1_hex_2));  // open: dp
  Hex_Digit_Display hex_digit_display_7 (.value(syscall_decoder_1_hex[7:4]));  // open: dp
  Button button_3 (.out(ExpSrc2));
  Hex_Digit_Display hex_digit_display_8 (.value(syscall_decoder_1_hex[3:0]));  // open: dp
  Multiplexer #(.width(32)) multiplexer_19 (
    .in0(alu_1_result), .in1(ram_1_dout), .out(multiplexer_19_out), .sel(MemtoReg));

  // Notes on the sheet:
  //   contents of ROMA (hex, n*v repeats v):
  //   20110001 8000c05 20110001 20120002 20130003 8000c09 20110001 20120002 20130003 8000c0d 20110001
  //   20120002 20130003 8000c11 20110001 20120002 20130003 c000d2e 20100001 20110001 118fc0 112020
  //   20020022 c 118882 12200001 8000c15 112020 20020022 c 20110001 118880 112020 20020022 c 12200001
  //   8000c1f 20110001 118fc0 112020 20020022 c 1188c3 112020 20020022 c 118903 112020 20020022 c 118903
  //   112020 20020022 c 118903 112020 20020022 c 118903 112020 20020022 c 118903 112020 20020022 c 118903
  //   112020 20020022 c 118903 112020 20020022 c 20100001 109fc0 139fc3 8021 2012000c 24160003 26100001
  //   3210000f 20080008 20090001 139900 2709825 132020 20020022 c 1094022 1500fff9 22100001 2018000f
  //   2188024 108700 20080008 20090001 139902 2709825 132021 20020022 c 1094022 1500fff9 108702 2c9b022
  //   12c00001 8000c50 4020 1084027 84400 3508ffff 82021 20020022 c 20110004 ae310000 8e320000 2252fffc
  //   20100000 22110001 2118020 22520004 ae500000 22310001 2118020 22520004 ae500000 22310001 2118020
  //   22520004 ae500000 22310001 2118020 22520004 ae500000 22310001 2118020 22520004 ae500000 22310001
  //   2118020 22520004 ae500000 22310001 2118020 22520004 ae500000 20090001 8c080004 1509008f ac000004
  //   20090003 8c080008 1509008b ac000008 20090006 8c08000c 15090087 ac00000c 2009000a 8c080010 15090083
  //   ac000010 2009000f 8c080014 1509007f ac000014 20090015 8c080018 1509007b ac000018 2009001c 8c08001c
  //   15090077 ac00001c 2010ffff 20110000 ae300000 22100001 22310004 ae300000 22100001 22310004 ae300000
  //   22100001 22310004 ae300000 22100001 22310004 ae300000 22100001 22310004 ae300000 22100001 22310004
  //   ae300000 22100001 22310004 ae300000 22100001 22310004 ae300000 22100001 22310004 ae300000 22100001
  //   22310004 ae300000 22100001 22310004 ae300000 22100001 22310004 ae300000 22100001 22310004 ae300000
  //   22100001 22310004 ae300000 22100001 22310004 ae300000 22100001 22310004 22100001 8020 2011003c
  //   8e130000 8e340000 274402a 11000002 ae330000 ae140000 2231fffc 1611fff8 102020 20020022 c 22100004
  //   2011003c 1611fff2 20100001 201200ff 20110001 20130003 12120005 12100004 20110001 20120002 20130003
  //   8000d26 102020 20020001 c 16310005 16320004 20110001 20120002 20130003 8000d26 132020 20020001 c
  //   2011ffff 118c00 2020 24840064 2484ff9c 14800017 2020 2484ff9c 24840064 14800013 2020 34847fff 912024
  //   1480000f 2020 34848000 912024 1480000b 24040000 8000d20 8000d26 2002000a c 20041ced 42400 3484cafe
  //   20020022 c 8000d1e 3c010000 3421baad 12020 42400 3484c0de 20020022 c 8000d1e 20100000 22100001
  //   102020 20020022 c 22100002 102020 20020022 c 22100003 102020 20020022 c 22100004 102020 20020022 c
  //   22100005 102020 20020022 c 22100006 102020 20020022 c 22100007 102020 20020022 c 22100008 102020
  //   20020022 c 3e00008
  //   contents of rom_1 (hex, n*v repeats v):
  //   201a0001 409a0800 201c0400 39df020 401a0000 afda0000 23de0004 23bd0004 401b1000 401a1800 409a1000
  //   afd00000 23bd0004 23de0004 afd40000 23bd0004 23de0004 afd50000 23bd0004 23de0004 afd60000 23bd0004
  //   23de0004 afc40000 23bd0004 23de0004 afc20000 23bd0004 23de0004 afdb0000 23bd0004 23de0004 1ab020
  //   22d60001 201a0000 409a0800 20140005 20150001 168020 102020 20020022 c 108100 1600fffb 295a022
  //   1680fff8 201a0001 409a0800 23defffc 23bdfffc 8fdb0000 23defffc 23bdfffc 8fc20000 23defffc 23bdfffc
  //   8fc40000 23defffc 23bdfffc 8fd60000 23defffc 23bdfffc 8fd50000 23defffc 23bdfffc 8fd40000 23defffc
  //   23bdfffc 8fd00000 409b1000 23defffc 23bdfffc 8fda0000 409a0000 201a0000 409a0800 42000018
endmodule
